# Fritzing sketch collar (saved by Fritzing 0.9.3b)
circuit board: 8.46667cm x 5.64444cm
perfboards: 1

parts:
  Part1 = Arduino Nano (Rev3.0)
  HC-SR04_Sensor_1 = HC-SR04 Ultrasonic Distance Sensor
  BUZZER = Piezo Speaker
  3V = Battery Holders [package=battcom_20mm_pth]
  3V_2 = Battery Holders [package=battcom_20mm_pth]
  3V_3 = Battery Holders [package=battcom_20mm_pth]

nets (from the breadboard view):
  GND: Part1.GND, HC-SR04_Sensor_1.GND, BUZZER.pin1, 3V.-
  N1: Part1.D8, BUZZER.pin2
  N2: Part1.D11/MOSI, HC-SR04_Sensor_1.ECHO
  N3: Part1.D12/MISO, HC-SR04_Sensor_1.TRIG
  N4: Part1.VIN, 3V_2.+
  5V: Part1.5V, HC-SR04_Sensor_1.VCC
  N5: 3V.+, 3V_3.-
  N6: 3V_2.-, 3V_3.+

notes:
  PROXIMITY SENSOR
  x3 COIN CELL
  blind-dog-collar
  Sara Aguado Couselo © 2019
